// Logisim project comp.circ as structural Verilog: 6 circuits, main circuit main
module main (
  output [7:0] out_1,
  output [7:0] out_2,
  output [3:0] out_3
);

  wire A_In, A_Out, adder_1_cout, Alu_Out, ALU_Subtract, B_In, B_Out, bintodec_1_out_2, bintodec_1_out_3,
       bintodec_1_out_4, bintodec_1_out_5, bintodec_1_out_6, bintodec_1_out_7, bintodec_1_out_8,
       bintodec_1_out_9, bintodec_1_out_10, bintodec_1_out_11, bintodec_1_out_12, bintodec_1_out_13,
       bintodec_1_out_14, bintodec_1_out_15, bintodec_1_out_16, bintodec_1_out_17, bintodec_1_out_18,
       bintodec_1_out_19, bintodec_1_out_20, bintodec_1_out_21, bintodec_1_out_22, bintodec_1_out_23,
       bintodec_1_out_24, bintodec_1_out_25, Carry_Bit, clock_1_out, clock_2_out, clock_3_out, clock_4_out,
       clock_5_out, clock_6_out, clock_7_out, clock_8_out, clock_10_out, Count_En, Count_Jump, Count_Out,
       decoder_1_out5, FLags_In, HLT, Instruction_In, Instruction_Out, Is_Carry, Is_Zero, not_1_out,
       or_1_out, Output_In, Ram_Adr_In, Ram_Data_In, Ram_Data_Out, RST, subtractor_1_bout, Zero_Bit;
  wire [2:0] counter_2_q;
  wire [3:0] Adr, Instructions, register_4_q;
  wire [7:0] A, adder_1_out, B, multiplexer_1_out, ram_1_dout, subtractor_1_out;

  Clock clock_1 (.out(clock_1_out));
  Clock clock_2 (.out(clock_2_out));
  Register register_1 (.D(out_2), .en(A_In), .clk(clock_1_out), .Q(A), .clr(RST));
  Clock clock_3 (.out(clock_3_out));
  not not_1 (not_1_out, clock_2_out);
  assign out_2 = A_Out ? A : 8'bz;  // Controlled_Buffer controlled_buffer_1
  Counter #(.max('hf), .width(4)) counter_1 (
    .load(Count_Jump), .D(out_2[3:0]), .count(Count_En), .Q(out_3), .clk(clock_4_out), .clr(RST));  // open: carry, up
  Clock clock_4 (.out(clock_4_out));
  Register #(.width(4)) register_2 (.D(out_2[3:0]), .en(Ram_Adr_In), .clk(clock_3_out), .Q(Adr), .clr(RST));
  Counter #(.max('h7), .width(3)) counter_2 (
    .Q(counter_2_q), .clk(not_1_out), .clr(or_1_out));  // open: load, D, count, carry, up
  or or_1 (or_1_out, RST, decoder_1_out5);
  Decoder #(.select(3)) decoder_1 (
    .out5(decoder_1_out5), .sel(counter_2_q));  // open: out0, out1, out2, out3, out4, out6, out7, en
  ROM #(.addrWidth(9), .dataWidth(16)) rom_1 (
    .addr({Instructions, counter_2_q, Is_Zero, Is_Carry}),
    .data({A_In, A_Out, B_In, FLags_In, ALU_Subtract, Alu_Out, Count_En, Count_Out, Count_Jump, Instruction_In, Instruction_Out, Ram_Adr_In, Ram_Data_In, Ram_Data_Out, Output_In, HLT}));
  assign out_2 = Count_Out ? {4'b0000, out_3} : 8'bz;  // Controlled_Buffer controlled_buffer_2
  Register register_3 (.D(out_2), .en(B_In), .clk(clock_5_out), .Q(B), .clr(RST));
  Clock clock_5 (.out(clock_5_out));
  RAM #(.addrWidth(4), .asyncread("true")) ram_1 (
    .addr(Adr), .we(Ram_Data_In), .clk(clock_6_out), .din(out_2), .dout(ram_1_dout));  // open: oe
  Clock clock_6 (.out(clock_6_out));
  assign out_2 = B_Out ? B : 8'bz;  // Controlled_Buffer controlled_buffer_3
  Adder adder_1 (.a(A), .b(B), .out(adder_1_out), .cout(adder_1_cout));  // open: cin
  Subtractor subtractor_1 (.a(A), .b(B), .out(subtractor_1_out), .bout(subtractor_1_bout));  // open: bin
  Multiplexer #(.width(8)) multiplexer_1 (
    .in0(adder_1_out), .in1(subtractor_1_out), .out(multiplexer_1_out), .sel(ALU_Subtract));
  assign out_2 = Ram_Data_Out ? ram_1_dout : 8'bz;  // Controlled_Buffer controlled_buffer_4
  assign out_2 = Alu_Out ? multiplexer_1_out : 8'bz;  // Controlled_Buffer controlled_buffer_5
  Register register_4 (.D(out_2), .en(Instruction_In), .clk(clock_7_out), .Q({Instructions, register_4_q}), .clr(RST));
  Clock clock_7 (.out(clock_7_out));
  assign out_2 = Instruction_Out ? {4'b0000, register_4_q} : 8'bz;  // Controlled_Buffer controlled_buffer_6
  nor nor_1 (Zero_Bit, multiplexer_1_out[0], multiplexer_1_out[1], multiplexer_1_out[2], multiplexer_1_out[3], multiplexer_1_out[4], multiplexer_1_out[5], multiplexer_1_out[6], multiplexer_1_out[7]);
  Multiplexer multiplexer_2 (.in0(adder_1_cout), .in1(subtractor_1_bout), .out(Carry_Bit), .sel(ALU_Subtract));
  Register register_5 (.D(out_2), .en(Output_In), .clk(clock_8_out), .Q(out_1), .clr(RST));
  Clock clock_8 (.out(clock_8_out));
  Button button_1 (.out(RST));
  LED led_1 (.in(HLT));
  Clock clock_9 ();  // open: out
  Register #(.width(2)) register_6 (
    .D({Carry_Bit, Zero_Bit}), .en(FLags_In), .clk(clock_10_out), .Q({Is_Zero, Is_Carry}), .clr(RST));
  Clock clock_10 (.out(clock_10_out));
  _7_Segment_Display u_7_segment_display_1 (
    .g(bintodec_1_out_2), .f(bintodec_1_out_3), .a(bintodec_1_out_4), .b(bintodec_1_out_5),
    .e(bintodec_1_out_6), .d(bintodec_1_out_7), .c(bintodec_1_out_8), .dp(bintodec_1_out_9));
  _7_Segment_Display u_7_segment_display_2 (
    .g(bintodec_1_out_10), .f(bintodec_1_out_11), .a(bintodec_1_out_12), .b(bintodec_1_out_13),
    .e(bintodec_1_out_14), .d(bintodec_1_out_15), .c(bintodec_1_out_16), .dp(bintodec_1_out_17));
  BinToDec bintodec_1 (
    .in_1(out_1), .out_2(bintodec_1_out_2), .out_10(bintodec_1_out_10), .out_18(bintodec_1_out_18),
    .out_3(bintodec_1_out_3), .out_11(bintodec_1_out_11), .out_19(bintodec_1_out_19),
    .out_4(bintodec_1_out_4), .out_12(bintodec_1_out_12), .out_20(bintodec_1_out_20),
    .out_5(bintodec_1_out_5), .out_13(bintodec_1_out_13), .out_21(bintodec_1_out_21),
    .out_6(bintodec_1_out_6), .out_14(bintodec_1_out_14), .out_22(bintodec_1_out_22),
    .out_7(bintodec_1_out_7), .out_15(bintodec_1_out_15), .out_23(bintodec_1_out_23),
    .out_8(bintodec_1_out_8), .out_16(bintodec_1_out_16), .out_24(bintodec_1_out_24),
    .out_9(bintodec_1_out_9), .out_17(bintodec_1_out_17), .out_25(bintodec_1_out_25));
  _7_Segment_Display u_7_segment_display_3 (
    .g(bintodec_1_out_18), .f(bintodec_1_out_19), .a(bintodec_1_out_20), .b(bintodec_1_out_21),
    .e(bintodec_1_out_22), .d(bintodec_1_out_23), .c(bintodec_1_out_24), .dp(bintodec_1_out_25));

  // Other names for the same wires on the sheet: B_U_S[7:0] = out_2; Count[3:0] = out_3; ANS[7:0] = out_1

  // Notes on the sheet:
  //   A Register
  //   Memory Adr Register
  //   Counter
  //   contents of rom_1 (hex, n*v repeats v):
  //   4*110 4*244 24*0 4*110 4*244 4*30 4*8004 16*0 4*110 4*244 4*30 4*2004 4*9400 12*0 4*110 4*244 4*30
  //   4*2004 4*9c00 12*0 4*110 4*244 4*30 4*4008 16*0 4*110 4*244 4*8020 20*0 4*110 4*244 4*a0 20*0 4*110
  //   4*244 0 0 a0 a0 20*0 4*110 4*244 0 a0 0 a0 20*0 4*110 4*244 24*0 4*110 4*244 24*0 4*110 4*244 24*0
  //   4*110 4*244 24*0 4*110 4*244 24*0 4*110 4*244 4*4002 20*0 4*110 4*244 4*1
  //   B Register
  //   Control Logic
  //   RAM
  //   ALU
  //   Instruction Register
  //   Output Register
  //   Flags Register
endmodule

module BinToDec (
  input  [7:0] in_1,
  output out_2,
  output out_3,
  output out_4,
  output out_5,
  output out_6,
  output out_7,
  output out_8,
  output out_9,
  output out_10,
  output out_11,
  output out_12,
  output out_13,
  output out_14,
  output out_15,
  output out_16,
  output out_17,
  output out_18,
  output out_19,
  output out_20,
  output out_21,
  output out_22,
  output out_23,
  output out_24,
  output out_25
);

  wire [3:0] X, Y, Z;
  wire [7:0] multiplier_1_out, multiplier_2_out, subtractor_1_out;
  wire [7:4] divider_1_out, divider_2_out, subtractor_2_out;

  Divider divider_1 (.a(in_1), .b(8'h64), .out({divider_1_out, X}));  // open: upper, rem
  ROM #(.addrWidth(4)) rom_1 (.addr(X), .data({out_9, out_8, out_7, out_6, out_5, out_4, out_3, out_2}));
  ROM #(.addrWidth(4)) rom_2 (.addr(Y), .data({out_17, out_16, out_15, out_14, out_13, out_12, out_11, out_10}));
  ROM #(.addrWidth(4)) rom_3 (.addr(Z), .data({out_25, out_24, out_23, out_22, out_21, out_20, out_19, out_18}));
  Multiplier multiplier_1 (.a({divider_1_out, X}), .b(8'h64), .out(multiplier_1_out));  // open: cin, cout
  Subtractor subtractor_1 (.a(in_1), .b(multiplier_1_out), .out(subtractor_1_out));  // open: bin, bout
  Divider divider_2 (.a(subtractor_1_out), .b(8'ha), .out({divider_2_out, Y}));  // open: upper, rem
  Multiplier multiplier_2 (.a({divider_2_out, Y}), .b(8'ha), .out(multiplier_2_out));  // open: cin, cout
  Subtractor subtractor_2 (.a(subtractor_1_out), .b(multiplier_2_out), .out({subtractor_2_out, Z}));  // open: bin, bout

  // Notes on the sheet:
  //   contents of rom_1 (hex, n*v repeats v):
  //   7e 48 3d 6d 4b 67 77 4c 7f 6f
  //   contents of rom_2 (hex, n*v repeats v):
  //   7e 48 3d 6d 4b 67 77 4c 7f 6f
  //   contents of rom_3 (hex, n*v repeats v):
  //   7e 48 3d 6d 4b 67 77 4c 7f 6f
endmodule

module Fetch_Writer (
  input  [2:0] in_1,
  input  [7:0] in_2,
  input  [7:0] in_3,
  output [5:0] out_4,
  output [3:0] out_5,
  output [1:0] out_6
);

  wire A_In, A_Out, Alu_Out, ALU_Subtract, B_In, button_1_out, button_2_out, Count_En, Count_Jump, Count_Out,
       FLags_In, HLT, Instruction_In, Instruction_Out, not_1_out, Output_In, Ram_Adr_In, Ram_Data_In,
       Ram_Data_Out;

  Button button_1 (.out(button_1_out));
  Counter #(.max('h3f), .width(6)) counter_1 (
    .Q(out_4), .clk(button_1_out), .clr(button_2_out));  // open: load, D, count, carry, up
  Button button_2 (.out(button_2_out));
  not not_1 (not_1_out, button_1_out);
  RAM #(.addrWidth(9), .asyncread("true"), .dataWidth(16)) ram_1 (
    .addr({out_4[5:2], in_1, out_4[1:0]}), .we(1'b1), .oe(1'b1), .clk(not_1_out), .din({in_2, in_3}),
    .dout({A_In, A_Out, B_In, FLags_In, ALU_Subtract, Alu_Out, Count_En, Count_Out, Count_Jump, Instruction_In, Instruction_Out, Ram_Adr_In, Ram_Data_In, Ram_Data_Out, Output_In, HLT}));

  assign out_5 = out_4[5:2];
  assign out_6 = out_4[1:0];
endmodule

module Command_Writer (
  input  [3:0] in_1,
  input  [2:0] in_2,
  input  [1:0] in_3,
  input  [7:0] in_4,
  input  [7:0] in_5
);

  wire A_In, A_Out, Alu_Out, ALU_Subtract, B_In, button_1_out, Count_En, Count_Jump, Count_Out, FLags_In,
       HLT, Instruction_In, Instruction_Out, Output_In, Ram_Adr_In, Ram_Data_In, Ram_Data_Out;

  Button button_1 (.out(button_1_out));
  RAM #(.addrWidth(9), .asyncread("true"), .dataWidth(16)) ram_1 (
    .addr({in_1, in_2, in_3}), .we(1'b1), .oe(1'b1), .clk(button_1_out), .din({in_4, in_5}),
    .dout({A_In, A_Out, B_In, FLags_In, ALU_Subtract, Alu_Out, Count_En, Count_Out, Count_Jump, Instruction_In, Instruction_Out, Ram_Adr_In, Ram_Data_In, Ram_Data_Out, Output_In, HLT}));
endmodule

module Programmer (
  input  [3:0] in_1,
  input  [3:0] in_2,
  input  [3:0] in_3,
  output [7:0] out_4
);

  wire button_1_out;

  Button button_1 (.out(button_1_out));
  RAM #(.addrWidth(4), .asyncread("true")) ram_1 (
    .addr(in_1), .we(1'b1), .oe(1'b1), .clk(button_1_out), .din({in_2, in_3}), .dout(out_4));
endmodule

module Temp (
  input  [1:0] in_1,
  input  [2:0] in_2,
  input  [3:0] in_3
);

  wire [1:0] undriven;
  wire [2:0] undriven_2;
  wire [3:0] undriven_3;

  ROM #(.addrWidth(9), .dataWidth(16)) rom_1 (.addr({undriven_3, undriven_2, undriven}));  // open: data

  // Notes on the sheet:
  //   contents of rom_1 (hex, n*v repeats v):
  //   4*110 4*244 24*0 4*110 4*244 4*30 4*8004 16*0 4*110 4*244 4*30 4*2004 4*9400 12*0 4*110 4*244 4*30
  //   4*2004 4*9c00 12*0 4*110 4*244 4*30 4*4008 16*0 4*110 4*244 4*8020 20*0 4*110 4*244 4*a0 20*0 4*110
  //   4*244 0 0 a0 a0 20*0 4*110 4*244 0 a0 0 a0 20*0 4*110 4*244 24*0 4*110 4*244 24*0 4*110 4*244 24*0
  //   4*110 4*244 24*0 4*110 4*244 24*0 4*110 4*244 4*4002 20*0 4*110 4*244 4*1
endmodule
